// Digital circuit fpu.dig as structural Verilog
module fpu (
);

  Register #(.Bits(32)) AL ();  // open: D, C, en, Q
  Register #(.Bits(32)) AH ();  // open: D, C, en, Q
  Register #(.Bits(32)) BL ();  // open: D, C, en, Q
  Register #(.Bits(32)) BH ();  // open: D, C, en, Q
  Register #(.Bits(32)) DL ();  // open: D, C, en, Q
  Register #(.Bits(32)) DH ();  // open: D, C, en, Q
  Register #(.Bits(32)) FL ();  // open: D, C, en, Q
  Register #(.Bits(32)) FH ();  // open: D, C, en, Q
  Register #(.Bits(12)) EA ();  // open: D, C, en, Q
  Register #(.Bits(12)) EB ();  // open: D, C, en, Q
  Register #(.Bits(6)) C ();  // open: D, C, en, Q
  Register #(.Bits(7)) SP ();  // open: D, C, en, Q
  Register #(.Bits(10), .isProgramCounter("true")) UPC ();  // open: D, C, en, Q
endmodule
